# Fritzing sketch ProMicroImplementation.fzpz (saved by Fritzing 0.9.6b)

parts:
  Part1 = Arduino Pro Micro (Clone)
  S1 = Toggle Switch [package=THT]
  JP1 = Header 3 [package=molex-1x3_lock]
  R1 = Resistor [tolerance=±5% power=0.25 resistance=10k package=THT]
  Part2 = ws2812b [package="smd 2812b"]

nets:
  N1: Part1.RXI, JP1.3
  GND: Part1.GND, JP1.1, R1.Pin_0, Part2.VSS
  N2: Part1.D3, S1.L1, R1.Pin_1
  N3: Part1.D5, Part2.DIN
  VCC: Part1.VCC, S1.COM, Part2.VDD
  N4: S1.L2, JP1.2
